// Logisim project alu-control.circ as structural Verilog: 1 circuit, main circuit main
module main (
  input  [5:0] Opcode,
  input  [5:0] Funct,
  output [3:0] Switch
);


  // Notes on the sheet:
  //   DO NOT MOVE, CHANGE, ADD, OR REMOVE INPUTS AND OUTPUTS!!!
endmodule
